# Fritzing sketch layout (saved by Fritzing 0.9.2b)
breadboards: 1

parts:
  Arduino = Arduino Uno (Rev3)
  Photocell = Photocell (LDR) [package=THT]
  Resistance = Resistor [tolerance=±0.05% resistance=10k package=THT]

nets:
  N1: Arduino.A0, Photocell.pin_1, Resistance.Pin_0
  N2: Arduino.5V, Photocell.pin_0
  N3: Arduino.GND, Resistance.Pin_1
